// Logisim project Битовые сдвиги.circ as structural Verilog: 3 circuits, main circuit main
module main (
  input  [7:0] Inp,
  input  [1:0] Method,
  input  Left_Right,
  input  [2:0] Shift,
  output [7:0] Ans
);

  wire all_shift_2_s0, all_shift_2_s1, all_shift_2_s2, all_shift_2_s3, all_shift_2_s4, all_shift_2_s5,
       all_shift_2_s6, all_shift_2_s7, all_shift_3_s0, all_shift_3_s1, all_shift_3_s2, all_shift_3_s3,
       all_shift_3_s4, all_shift_3_s5, all_shift_3_s6, all_shift_3_s7, all_shift_4_s0, all_shift_4_s1,
       all_shift_4_s2, all_shift_4_s3, all_shift_4_s4, all_shift_4_s5, all_shift_4_s6, all_shift_4_s7,
       all_shift_5_s0, all_shift_5_s1, all_shift_5_s2, all_shift_5_s3, all_shift_5_s4, all_shift_5_s5,
       all_shift_5_s6, all_shift_5_s7, all_shift_6_s0, all_shift_6_s1, all_shift_6_s2, all_shift_6_s3,
       all_shift_6_s4, all_shift_6_s5, all_shift_6_s6, all_shift_6_s7, all_shift_7_s0, all_shift_7_s1,
       all_shift_7_s2, all_shift_7_s3, all_shift_7_s4, all_shift_7_s5, all_shift_7_s6, all_shift_7_s7,
       all_shift_9_s0, all_shift_9_s1, all_shift_9_s2, all_shift_9_s3, all_shift_9_s4, all_shift_9_s5,
       all_shift_9_s6, all_shift_9_s7, all_shift_10_s0, all_shift_10_s1, all_shift_10_s2, all_shift_10_s3,
       all_shift_10_s4, all_shift_10_s5, all_shift_10_s6, all_shift_10_s7, all_shift_11_s0, all_shift_11_s1,
       all_shift_11_s2, all_shift_11_s3, all_shift_11_s4, all_shift_11_s5, all_shift_11_s6, all_shift_11_s7,
       all_shift_12_s0, all_shift_12_s1, all_shift_12_s2, all_shift_12_s3, all_shift_12_s4, all_shift_12_s5,
       all_shift_12_s6, all_shift_12_s7, all_shift_13_s0, all_shift_13_s1, all_shift_13_s2, all_shift_13_s3,
       all_shift_13_s4, all_shift_13_s5, all_shift_13_s6, all_shift_13_s7, all_shift_15_s0, all_shift_15_s1,
       all_shift_15_s2, all_shift_15_s3, all_shift_15_s4, all_shift_15_s5, all_shift_15_s6, all_shift_15_s7,
       all_shift_16_s0, all_shift_16_s1, all_shift_16_s2, all_shift_16_s3, all_shift_16_s4, all_shift_16_s5,
       all_shift_16_s6, all_shift_16_s7, all_shift_17_s0, all_shift_17_s1, all_shift_17_s2, all_shift_17_s3,
       all_shift_17_s4, all_shift_17_s5, all_shift_17_s6, all_shift_17_s7, all_shift_18_s0, all_shift_18_s1,
       all_shift_18_s2, all_shift_18_s3, all_shift_18_s4, all_shift_18_s5, all_shift_18_s6, all_shift_18_s7,
       all_shift_20_s0, all_shift_20_s1, all_shift_20_s2, all_shift_20_s3, all_shift_20_s4, all_shift_20_s5,
       all_shift_20_s6, all_shift_20_s7, all_shift_21_s0, all_shift_21_s1, all_shift_21_s2, all_shift_21_s3,
       all_shift_21_s4, all_shift_21_s5, all_shift_21_s6, all_shift_21_s7, all_shift_22_s0, all_shift_22_s1,
       all_shift_22_s2, all_shift_22_s3, all_shift_22_s4, all_shift_22_s5, all_shift_22_s6, all_shift_22_s7,
       all_shift_24_s0, all_shift_24_s1, all_shift_24_s2, all_shift_24_s3, all_shift_24_s4, all_shift_24_s5,
       all_shift_24_s6, all_shift_24_s7, all_shift_25_s0, all_shift_25_s1, all_shift_25_s2, all_shift_25_s3,
       all_shift_25_s4, all_shift_25_s5, all_shift_25_s6, all_shift_25_s7, all_shift_27_s0, all_shift_27_s1,
       all_shift_27_s2, all_shift_27_s3, all_shift_27_s4, all_shift_27_s5, all_shift_27_s6, all_shift_27_s7,
       not_1_out;
  wire [7:0] all_shift_1_s0, all_shift_8_s0, all_shift_14_s0, all_shift_19_s0, all_shift_23_s0,
       all_shift_26_s0, all_shift_28_s0;

  not not_1 (not_1_out, Left_Right);
  all_shift all_shift_1 (
    .D0(Inp[0]), .D1(Inp[1]), .D2(Inp[2]), .D3(Inp[3]), .D4(Inp[4]), .D5(Inp[5]), .D6(Inp[6]), .D7(Inp[7]),
    .Left_Right(not_1_out), .Method(Method), .neg(Inp[7]), .S0(all_shift_1_s0[0]), .S1(all_shift_1_s0[1]),
    .S2(all_shift_1_s0[2]), .S3(all_shift_1_s0[3]), .S4(all_shift_1_s0[4]), .S5(all_shift_1_s0[5]),
    .S6(all_shift_1_s0[6]), .S7(all_shift_1_s0[7]));
  all_shift all_shift_2 (
    .D0(Inp[0]), .D1(Inp[1]), .D2(Inp[2]), .D3(Inp[3]), .D4(Inp[4]), .D5(Inp[5]), .D6(Inp[6]), .D7(Inp[7]),
    .Left_Right(not_1_out), .Method(Method), .neg(Inp[7]), .S0(all_shift_2_s0), .S1(all_shift_2_s1),
    .S2(all_shift_2_s2), .S3(all_shift_2_s3), .S4(all_shift_2_s4), .S5(all_shift_2_s5), .S6(all_shift_2_s6),
    .S7(all_shift_2_s7));
  all_shift all_shift_3 (
    .D0(Inp[0]), .D1(Inp[1]), .D2(Inp[2]), .D3(Inp[3]), .D4(Inp[4]), .D5(Inp[5]), .D6(Inp[6]), .D7(Inp[7]),
    .Left_Right(not_1_out), .Method(Method), .neg(Inp[7]), .S0(all_shift_3_s0), .S1(all_shift_3_s1),
    .S2(all_shift_3_s2), .S3(all_shift_3_s3), .S4(all_shift_3_s4), .S5(all_shift_3_s5), .S6(all_shift_3_s6),
    .S7(all_shift_3_s7));
  all_shift all_shift_4 (
    .D0(Inp[0]), .D1(Inp[1]), .D2(Inp[2]), .D3(Inp[3]), .D4(Inp[4]), .D5(Inp[5]), .D6(Inp[6]), .D7(Inp[7]),
    .Left_Right(not_1_out), .Method(Method), .neg(Inp[7]), .S0(all_shift_4_s0), .S1(all_shift_4_s1),
    .S2(all_shift_4_s2), .S3(all_shift_4_s3), .S4(all_shift_4_s4), .S5(all_shift_4_s5), .S6(all_shift_4_s6),
    .S7(all_shift_4_s7));
  all_shift all_shift_5 (
    .D0(Inp[0]), .D1(Inp[1]), .D2(Inp[2]), .D3(Inp[3]), .D4(Inp[4]), .D5(Inp[5]), .D6(Inp[6]), .D7(Inp[7]),
    .Left_Right(not_1_out), .Method(Method), .neg(Inp[7]), .S0(all_shift_5_s0), .S1(all_shift_5_s1),
    .S2(all_shift_5_s2), .S3(all_shift_5_s3), .S4(all_shift_5_s4), .S5(all_shift_5_s5), .S6(all_shift_5_s6),
    .S7(all_shift_5_s7));
  all_shift all_shift_6 (
    .D0(Inp[0]), .D1(Inp[1]), .D2(Inp[2]), .D3(Inp[3]), .D4(Inp[4]), .D5(Inp[5]), .D6(Inp[6]), .D7(Inp[7]),
    .Left_Right(not_1_out), .Method(Method), .neg(Inp[7]), .S0(all_shift_6_s0), .S1(all_shift_6_s1),
    .S2(all_shift_6_s2), .S3(all_shift_6_s3), .S4(all_shift_6_s4), .S5(all_shift_6_s5), .S6(all_shift_6_s6),
    .S7(all_shift_6_s7));
  all_shift all_shift_7 (
    .D0(Inp[0]), .D1(Inp[1]), .D2(Inp[2]), .D3(Inp[3]), .D4(Inp[4]), .D5(Inp[5]), .D6(Inp[6]), .D7(Inp[7]),
    .Left_Right(not_1_out), .Method(Method), .neg(Inp[7]), .S0(all_shift_7_s0), .S1(all_shift_7_s1),
    .S2(all_shift_7_s2), .S3(all_shift_7_s3), .S4(all_shift_7_s4), .S5(all_shift_7_s5), .S6(all_shift_7_s6),
    .S7(all_shift_7_s7));
  all_shift all_shift_8 (
    .D0(all_shift_2_s0), .D1(all_shift_2_s1), .D2(all_shift_2_s2), .D3(all_shift_2_s3), .D4(all_shift_2_s4),
    .D5(all_shift_2_s5), .D6(all_shift_2_s6), .D7(all_shift_2_s7), .Left_Right(not_1_out), .Method(Method),
    .neg(Inp[7]), .S0(all_shift_8_s0[0]), .S1(all_shift_8_s0[1]), .S2(all_shift_8_s0[2]),
    .S3(all_shift_8_s0[3]), .S4(all_shift_8_s0[4]), .S5(all_shift_8_s0[5]), .S6(all_shift_8_s0[6]),
    .S7(all_shift_8_s0[7]));
  all_shift all_shift_9 (
    .D0(all_shift_3_s0), .D1(all_shift_3_s1), .D2(all_shift_3_s2), .D3(all_shift_3_s3), .D4(all_shift_3_s4),
    .D5(all_shift_3_s5), .D6(all_shift_3_s6), .D7(all_shift_3_s7), .Left_Right(not_1_out), .Method(Method),
    .neg(Inp[7]), .S0(all_shift_9_s0), .S1(all_shift_9_s1), .S2(all_shift_9_s2), .S3(all_shift_9_s3),
    .S4(all_shift_9_s4), .S5(all_shift_9_s5), .S6(all_shift_9_s6), .S7(all_shift_9_s7));
  all_shift all_shift_10 (
    .D0(all_shift_4_s0), .D1(all_shift_4_s1), .D2(all_shift_4_s2), .D3(all_shift_4_s3), .D4(all_shift_4_s4),
    .D5(all_shift_4_s5), .D6(all_shift_4_s6), .D7(all_shift_4_s7), .Left_Right(not_1_out), .Method(Method),
    .neg(Inp[7]), .S0(all_shift_10_s0), .S1(all_shift_10_s1), .S2(all_shift_10_s2), .S3(all_shift_10_s3),
    .S4(all_shift_10_s4), .S5(all_shift_10_s5), .S6(all_shift_10_s6), .S7(all_shift_10_s7));
  all_shift all_shift_11 (
    .D0(all_shift_5_s0), .D1(all_shift_5_s1), .D2(all_shift_5_s2), .D3(all_shift_5_s3), .D4(all_shift_5_s4),
    .D5(all_shift_5_s5), .D6(all_shift_5_s6), .D7(all_shift_5_s7), .Left_Right(not_1_out), .Method(Method),
    .neg(Inp[7]), .S0(all_shift_11_s0), .S1(all_shift_11_s1), .S2(all_shift_11_s2), .S3(all_shift_11_s3),
    .S4(all_shift_11_s4), .S5(all_shift_11_s5), .S6(all_shift_11_s6), .S7(all_shift_11_s7));
  all_shift all_shift_12 (
    .D0(all_shift_6_s0), .D1(all_shift_6_s1), .D2(all_shift_6_s2), .D3(all_shift_6_s3), .D4(all_shift_6_s4),
    .D5(all_shift_6_s5), .D6(all_shift_6_s6), .D7(all_shift_6_s7), .Left_Right(not_1_out), .Method(Method),
    .neg(Inp[7]), .S0(all_shift_12_s0), .S1(all_shift_12_s1), .S2(all_shift_12_s2), .S3(all_shift_12_s3),
    .S4(all_shift_12_s4), .S5(all_shift_12_s5), .S6(all_shift_12_s6), .S7(all_shift_12_s7));
  all_shift all_shift_13 (
    .D0(all_shift_7_s0), .D1(all_shift_7_s1), .D2(all_shift_7_s2), .D3(all_shift_7_s3), .D4(all_shift_7_s4),
    .D5(all_shift_7_s5), .D6(all_shift_7_s6), .D7(all_shift_7_s7), .Left_Right(not_1_out), .Method(Method),
    .neg(Inp[7]), .S0(all_shift_13_s0), .S1(all_shift_13_s1), .S2(all_shift_13_s2), .S3(all_shift_13_s3),
    .S4(all_shift_13_s4), .S5(all_shift_13_s5), .S6(all_shift_13_s6), .S7(all_shift_13_s7));
  all_shift all_shift_14 (
    .D0(all_shift_9_s0), .D1(all_shift_9_s1), .D2(all_shift_9_s2), .D3(all_shift_9_s3), .D4(all_shift_9_s4),
    .D5(all_shift_9_s5), .D6(all_shift_9_s6), .D7(all_shift_9_s7), .Left_Right(not_1_out), .Method(Method),
    .neg(Inp[7]), .S0(all_shift_14_s0[0]), .S1(all_shift_14_s0[1]), .S2(all_shift_14_s0[2]),
    .S3(all_shift_14_s0[3]), .S4(all_shift_14_s0[4]), .S5(all_shift_14_s0[5]), .S6(all_shift_14_s0[6]),
    .S7(all_shift_14_s0[7]));
  all_shift all_shift_15 (
    .D0(all_shift_10_s0), .D1(all_shift_10_s1), .D2(all_shift_10_s2), .D3(all_shift_10_s3),
    .D4(all_shift_10_s4), .D5(all_shift_10_s5), .D6(all_shift_10_s6), .D7(all_shift_10_s7),
    .Left_Right(not_1_out), .Method(Method), .neg(Inp[7]), .S0(all_shift_15_s0), .S1(all_shift_15_s1),
    .S2(all_shift_15_s2), .S3(all_shift_15_s3), .S4(all_shift_15_s4), .S5(all_shift_15_s5),
    .S6(all_shift_15_s6), .S7(all_shift_15_s7));
  all_shift all_shift_16 (
    .D0(all_shift_11_s0), .D1(all_shift_11_s1), .D2(all_shift_11_s2), .D3(all_shift_11_s3),
    .D4(all_shift_11_s4), .D5(all_shift_11_s5), .D6(all_shift_11_s6), .D7(all_shift_11_s7),
    .Left_Right(not_1_out), .Method(Method), .neg(Inp[7]), .S0(all_shift_16_s0), .S1(all_shift_16_s1),
    .S2(all_shift_16_s2), .S3(all_shift_16_s3), .S4(all_shift_16_s4), .S5(all_shift_16_s5),
    .S6(all_shift_16_s6), .S7(all_shift_16_s7));
  all_shift all_shift_17 (
    .D0(all_shift_12_s0), .D1(all_shift_12_s1), .D2(all_shift_12_s2), .D3(all_shift_12_s3),
    .D4(all_shift_12_s4), .D5(all_shift_12_s5), .D6(all_shift_12_s6), .D7(all_shift_12_s7),
    .Left_Right(not_1_out), .Method(Method), .neg(Inp[7]), .S0(all_shift_17_s0), .S1(all_shift_17_s1),
    .S2(all_shift_17_s2), .S3(all_shift_17_s3), .S4(all_shift_17_s4), .S5(all_shift_17_s5),
    .S6(all_shift_17_s6), .S7(all_shift_17_s7));
  all_shift all_shift_18 (
    .D0(all_shift_13_s0), .D1(all_shift_13_s1), .D2(all_shift_13_s2), .D3(all_shift_13_s3),
    .D4(all_shift_13_s4), .D5(all_shift_13_s5), .D6(all_shift_13_s6), .D7(all_shift_13_s7),
    .Left_Right(not_1_out), .Method(Method), .neg(Inp[7]), .S0(all_shift_18_s0), .S1(all_shift_18_s1),
    .S2(all_shift_18_s2), .S3(all_shift_18_s3), .S4(all_shift_18_s4), .S5(all_shift_18_s5),
    .S6(all_shift_18_s6), .S7(all_shift_18_s7));
  all_shift all_shift_19 (
    .D0(all_shift_15_s0), .D1(all_shift_15_s1), .D2(all_shift_15_s2), .D3(all_shift_15_s3),
    .D4(all_shift_15_s4), .D5(all_shift_15_s5), .D6(all_shift_15_s6), .D7(all_shift_15_s7),
    .Left_Right(not_1_out), .Method(Method), .neg(Inp[7]), .S0(all_shift_19_s0[0]), .S1(all_shift_19_s0[1]),
    .S2(all_shift_19_s0[2]), .S3(all_shift_19_s0[3]), .S4(all_shift_19_s0[4]), .S5(all_shift_19_s0[5]),
    .S6(all_shift_19_s0[6]), .S7(all_shift_19_s0[7]));
  all_shift all_shift_20 (
    .D0(all_shift_16_s0), .D1(all_shift_16_s1), .D2(all_shift_16_s2), .D3(all_shift_16_s3),
    .D4(all_shift_16_s4), .D5(all_shift_16_s5), .D6(all_shift_16_s6), .D7(all_shift_16_s7),
    .Left_Right(not_1_out), .Method(Method), .neg(Inp[7]), .S0(all_shift_20_s0), .S1(all_shift_20_s1),
    .S2(all_shift_20_s2), .S3(all_shift_20_s3), .S4(all_shift_20_s4), .S5(all_shift_20_s5),
    .S6(all_shift_20_s6), .S7(all_shift_20_s7));
  all_shift all_shift_21 (
    .D0(all_shift_17_s0), .D1(all_shift_17_s1), .D2(all_shift_17_s2), .D3(all_shift_17_s3),
    .D4(all_shift_17_s4), .D5(all_shift_17_s5), .D6(all_shift_17_s6), .D7(all_shift_17_s7),
    .Left_Right(not_1_out), .Method(Method), .neg(Inp[7]), .S0(all_shift_21_s0), .S1(all_shift_21_s1),
    .S2(all_shift_21_s2), .S3(all_shift_21_s3), .S4(all_shift_21_s4), .S5(all_shift_21_s5),
    .S6(all_shift_21_s6), .S7(all_shift_21_s7));
  all_shift all_shift_22 (
    .D0(all_shift_18_s0), .D1(all_shift_18_s1), .D2(all_shift_18_s2), .D3(all_shift_18_s3),
    .D4(all_shift_18_s4), .D5(all_shift_18_s5), .D6(all_shift_18_s6), .D7(all_shift_18_s7),
    .Left_Right(not_1_out), .Method(Method), .neg(Inp[7]), .S0(all_shift_22_s0), .S1(all_shift_22_s1),
    .S2(all_shift_22_s2), .S3(all_shift_22_s3), .S4(all_shift_22_s4), .S5(all_shift_22_s5),
    .S6(all_shift_22_s6), .S7(all_shift_22_s7));
  Multiplexer #(.enable("false"), .select(3), .width(8)) multiplexer_1 (
    .in0(Inp), .in1(all_shift_1_s0), .in2(all_shift_8_s0), .in3(all_shift_14_s0), .in4(all_shift_19_s0),
    .in5(all_shift_23_s0), .in6(all_shift_26_s0), .in7(all_shift_28_s0), .out(Ans), .sel(Shift));
  all_shift all_shift_23 (
    .D0(all_shift_20_s0), .D1(all_shift_20_s1), .D2(all_shift_20_s2), .D3(all_shift_20_s3),
    .D4(all_shift_20_s4), .D5(all_shift_20_s5), .D6(all_shift_20_s6), .D7(all_shift_20_s7),
    .Left_Right(not_1_out), .Method(Method), .neg(Inp[7]), .S0(all_shift_23_s0[0]), .S1(all_shift_23_s0[1]),
    .S2(all_shift_23_s0[2]), .S3(all_shift_23_s0[3]), .S4(all_shift_23_s0[4]), .S5(all_shift_23_s0[5]),
    .S6(all_shift_23_s0[6]), .S7(all_shift_23_s0[7]));
  all_shift all_shift_24 (
    .D0(all_shift_21_s0), .D1(all_shift_21_s1), .D2(all_shift_21_s2), .D3(all_shift_21_s3),
    .D4(all_shift_21_s4), .D5(all_shift_21_s5), .D6(all_shift_21_s6), .D7(all_shift_21_s7),
    .Left_Right(not_1_out), .Method(Method), .neg(Inp[7]), .S0(all_shift_24_s0), .S1(all_shift_24_s1),
    .S2(all_shift_24_s2), .S3(all_shift_24_s3), .S4(all_shift_24_s4), .S5(all_shift_24_s5),
    .S6(all_shift_24_s6), .S7(all_shift_24_s7));
  all_shift all_shift_25 (
    .D0(all_shift_22_s0), .D1(all_shift_22_s1), .D2(all_shift_22_s2), .D3(all_shift_22_s3),
    .D4(all_shift_22_s4), .D5(all_shift_22_s5), .D6(all_shift_22_s6), .D7(all_shift_22_s7),
    .Left_Right(not_1_out), .Method(Method), .neg(Inp[7]), .S0(all_shift_25_s0), .S1(all_shift_25_s1),
    .S2(all_shift_25_s2), .S3(all_shift_25_s3), .S4(all_shift_25_s4), .S5(all_shift_25_s5),
    .S6(all_shift_25_s6), .S7(all_shift_25_s7));
  all_shift all_shift_26 (
    .D0(all_shift_24_s0), .D1(all_shift_24_s1), .D2(all_shift_24_s2), .D3(all_shift_24_s3),
    .D4(all_shift_24_s4), .D5(all_shift_24_s5), .D6(all_shift_24_s6), .D7(all_shift_24_s7),
    .Left_Right(not_1_out), .Method(Method), .neg(Inp[7]), .S0(all_shift_26_s0[0]), .S1(all_shift_26_s0[1]),
    .S2(all_shift_26_s0[2]), .S3(all_shift_26_s0[3]), .S4(all_shift_26_s0[4]), .S5(all_shift_26_s0[5]),
    .S6(all_shift_26_s0[6]), .S7(all_shift_26_s0[7]));
  all_shift all_shift_27 (
    .D0(all_shift_25_s0), .D1(all_shift_25_s1), .D2(all_shift_25_s2), .D3(all_shift_25_s3),
    .D4(all_shift_25_s4), .D5(all_shift_25_s5), .D6(all_shift_25_s6), .D7(all_shift_25_s7),
    .Left_Right(not_1_out), .Method(Method), .neg(Inp[7]), .S0(all_shift_27_s0), .S1(all_shift_27_s1),
    .S2(all_shift_27_s2), .S3(all_shift_27_s3), .S4(all_shift_27_s4), .S5(all_shift_27_s5),
    .S6(all_shift_27_s6), .S7(all_shift_27_s7));
  all_shift all_shift_28 (
    .D0(all_shift_27_s0), .D1(all_shift_27_s1), .D2(all_shift_27_s2), .D3(all_shift_27_s3),
    .D4(all_shift_27_s4), .D5(all_shift_27_s5), .D6(all_shift_27_s6), .D7(all_shift_27_s7),
    .Left_Right(not_1_out), .Method(Method), .neg(Inp[7]), .S0(all_shift_28_s0[0]), .S1(all_shift_28_s0[1]),
    .S2(all_shift_28_s0[2]), .S3(all_shift_28_s0[3]), .S4(all_shift_28_s0[4]), .S5(all_shift_28_s0[5]),
    .S6(all_shift_28_s0[6]), .S7(all_shift_28_s0[7]));
endmodule

module all_shift (
  input  D0,
  input  D1,
  input  D2,
  input  D3,
  input  D4,
  input  D5,
  input  D6,
  input  D7,
  input  Left_Right,
  input  [1:0] Method,
  input  neg,
  output S0,
  output S1,
  output S2,
  output S3,
  output S4,
  output S5,
  output S6,
  output S7
);

  wire and_1_out, and_2_out, and_3_out, and_4_out, and_5_out, and_6_out, and_7_out, and_8_out, and_9_out,
       and_10_out, and_11_out, and_12_out, and_13_out, and_14_out, and_15_out, and_16_out, and_17_out,
       and_18_out, and_19_out, multiplex_1_y, not_1_out, not_2_out, or_2_out;

  not not_1 (not_1_out, Left_Right);
  not not_2 (not_2_out, Left_Right);
  and and_1 (and_1_out, Left_Right, D7);
  and and_2 (and_2_out, not_2_out, neg);
  and and_3 (and_3_out, D0, Left_Right);
  or or_1 (S0, and_5_out, and_9_out);
  and and_4 (and_4_out, D0, not_2_out);
  or or_2 (or_2_out, and_4_out, and_1_out);
  and and_5 (and_5_out, not_1_out, D1);
  and and_6 (and_6_out, D1, Left_Right);
  or or_3 (S1, and_3_out, and_7_out);
  multiplex multiplex_1 (
    .A(1'b0), .B(and_2_out), .C(or_2_out), .S1(Method[1]), .S0(Method[0]), .Y(multiplex_1_y));  // open: D
  and and_7 (and_7_out, not_1_out, D2);
  and and_8 (and_8_out, D2, Left_Right);
  or or_4 (S2, and_6_out, and_10_out);
  and and_9 (and_9_out, multiplex_1_y, Left_Right);
  and and_10 (and_10_out, not_1_out, D3);
  or or_5 (S3, and_8_out, and_13_out);
  and and_11 (and_11_out, multiplex_1_y, not_1_out);
  and and_12 (and_12_out, D3, Left_Right);
  and and_13 (and_13_out, not_1_out, D4);
  and and_14 (and_14_out, D4, Left_Right);
  or or_6 (S4, and_12_out, and_15_out);
  and and_15 (and_15_out, not_1_out, D5);
  or or_7 (S5, and_14_out, and_18_out);
  and and_16 (and_16_out, D5, Left_Right);
  and and_17 (and_17_out, D6, Left_Right);
  and and_18 (and_18_out, not_1_out, D6);
  or or_8 (S6, and_16_out, and_19_out);
  and and_19 (and_19_out, not_1_out, D7);
  or or_9 (S7, and_17_out, and_11_out);
endmodule

module multiplex (
  input  A,
  input  B,
  input  C,
  input  D,
  input  S1,
  input  S0,
  output Y
);

  wire and_1_out, and_2_out, and_3_out, and_4_out, not_1_out, not_2_out;

  not not_1 (not_1_out, S1);
  not not_2 (not_2_out, S0);
  and and_1 (and_1_out, A, not_1_out, not_2_out);
  and and_2 (and_2_out, B, not_1_out, S0);
  and and_3 (and_3_out, C, S1, not_2_out);
  and and_4 (and_4_out, D, S1, S0);
  or or_1 (Y, and_1_out, and_2_out, and_3_out, and_4_out);
endmodule
