// Logisim project Вычитатель 8b.circ as structural Verilog: 2 circuits, main circuit main
module main (
  input  [7:0] A,
  input  [7:0] B,
  output [7:0] C
);

  wire sum_1_p, sum_2_p, sum_3_p, sum_4_p, sum_5_p, sum_6_p, sum_7_p, sum_8_p, xor_1_out, xor_2_out,
       xor_3_out, xor_4_out, xor_5_out, xor_6_out, xor_7_out, xor_8_out;

  sum sum_1 (.A(A[0]), .B(xor_8_out), .P0(1'b1), .S(C[0]), .P(sum_1_p));
  sum sum_2 (.A(A[4]), .B(xor_4_out), .P0(sum_7_p), .S(C[4]), .P(sum_2_p));
  xor xor_1 (xor_1_out, B[7], 1'b1);
  sum sum_3 (.A(A[1]), .B(xor_7_out), .P0(sum_1_p), .S(C[1]), .P(sum_3_p));
  sum sum_4 (.A(A[5]), .B(xor_3_out), .P0(sum_2_p), .S(C[5]), .P(sum_4_p));
  xor xor_2 (xor_2_out, B[6], 1'b1);
  xor xor_3 (xor_3_out, B[5], 1'b1);
  xor xor_4 (xor_4_out, B[4], 1'b1);
  xor xor_5 (xor_5_out, B[3], 1'b1);
  sum sum_5 (.A(A[2]), .B(xor_6_out), .P0(sum_3_p), .S(C[2]), .P(sum_5_p));
  sum sum_6 (.A(A[6]), .B(xor_2_out), .P0(sum_4_p), .S(C[6]), .P(sum_6_p));
  xor xor_6 (xor_6_out, B[2], 1'b1);
  xor xor_7 (xor_7_out, B[1], 1'b1);
  sum sum_7 (.A(A[3]), .B(xor_5_out), .P0(sum_5_p), .S(C[3]), .P(sum_7_p));
  sum sum_8 (.A(A[7]), .B(xor_1_out), .P0(sum_6_p), .S(C[7]), .P(sum_8_p));
  xor xor_8 (xor_8_out, B[0], 1'b1);
  LED led_1 (.in(sum_8_p));
endmodule

module sum (
  input  A,
  input  B,
  input  P0,
  output S,
  output P
);

  wire and_1_out, and_2_out, xor_1_out;

  and and_1 (and_1_out, A, B);
  xor xor_1 (xor_1_out, A, B);
  xor xor_2 (S, xor_1_out, P0);
  and and_2 (and_2_out, xor_1_out, P0);
  or or_1 (P, and_1_out, and_2_out);
endmodule
