// Logisim project Деление 8b усложненное.circ as structural Verilog: 4 circuits, main circuit DIV8
module main (
  input  [7:0] A,
  input  [7:0] B,
  output [7:0] C,
  output [7:0] D
);

  wire unsigned8_1_sign, unsigned8_2_sign, xor_1_out;
  wire [7:0] div8_1_quotient, div8_1_remainder, negator_1_out, negator_2_out, unsigned8_1_outp,
       unsigned8_2_outp;

  UNSIGNED8 unsigned8_1 (.inp(A), .outp(unsigned8_1_outp), .sign(unsigned8_1_sign));
  UNSIGNED8 unsigned8_2 (.inp(B), .outp(unsigned8_2_outp), .sign(unsigned8_2_sign));
  xor xor_1 (xor_1_out, unsigned8_1_sign, unsigned8_2_sign);
  DIV8 div8_1 (.A(unsigned8_1_outp), .B(unsigned8_2_outp), .Remainder(div8_1_remainder), .Quotient(div8_1_quotient));
  Negator negator_1 (.in(div8_1_quotient), .out(negator_1_out));
  Negator negator_2 (.in(div8_1_remainder), .out(negator_2_out));
  Multiplexer #(.enable("false"), .width(8)) multiplexer_1 (
    .in0(div8_1_quotient), .in1(negator_1_out), .out(C), .sel(xor_1_out));
  Multiplexer #(.enable("false"), .width(8)) multiplexer_2 (
    .in0(div8_1_remainder), .in1(negator_2_out), .out(D), .sel(unsigned8_1_sign));
endmodule

module UNSIGNED8 (
  input  [7:0] inp,
  output [7:0] outp,
  output sign
);

  wire [7:0] negator_1_out;

  BitSelector bitselector_1 (.in(inp), .out(sign), .sel(3'b111));
  Negator negator_1 (.in(inp), .out(negator_1_out));
  Multiplexer #(.enable("false"), .width(8)) multiplexer_1 (.in0(inp), .in1(negator_1_out), .out(outp), .sel(sign));
endmodule

module DIV8 (
  input  [7:0] A,
  input  [7:0] B,
  output [7:0] Remainder,
  output [7:0] Quotient
);

  wire comparator_1_eq;
  wire [7:0] condsub8_1_ans, condsub8_2_ans, condsub8_3_ans, condsub8_4_ans, condsub8_5_ans, condsub8_6_ans,
       condsub8_7_ans, condsub8_8_q;
  wire [15:0] bit_extender_1_out;

  assign bit_extender_1_out = {{8{1'b0}}, A};  // Bit_Extender bit_extender_1
  Comparator #(.mode("unsigned")) comparator_1 (.a(B), .b({8{1'b0}}), .eq(comparator_1_eq));  // open: gt, lt
  CONDSUB8 condsub8_1 (
    .A(bit_extender_1_out[15:8]), .B(B), .sign(bit_extender_1_out[7]), .Q(condsub8_8_q[7]),
    .ans(condsub8_1_ans));
  CONDSUB8 condsub8_2 (
    .A(condsub8_1_ans), .B(B), .sign(bit_extender_1_out[6]), .Q(condsub8_8_q[6]), .ans(condsub8_2_ans));
  CONDSUB8 condsub8_3 (
    .A(condsub8_2_ans), .B(B), .sign(bit_extender_1_out[5]), .Q(condsub8_8_q[5]), .ans(condsub8_3_ans));
  CONDSUB8 condsub8_4 (
    .A(condsub8_3_ans), .B(B), .sign(bit_extender_1_out[4]), .Q(condsub8_8_q[4]), .ans(condsub8_4_ans));
  CONDSUB8 condsub8_5 (
    .A(condsub8_4_ans), .B(B), .sign(bit_extender_1_out[3]), .Q(condsub8_8_q[3]), .ans(condsub8_5_ans));
  CONDSUB8 condsub8_6 (
    .A(condsub8_5_ans), .B(B), .sign(bit_extender_1_out[2]), .Q(condsub8_8_q[2]), .ans(condsub8_6_ans));
  CONDSUB8 condsub8_7 (
    .A(condsub8_6_ans), .B(B), .sign(bit_extender_1_out[1]), .Q(condsub8_8_q[1]), .ans(condsub8_7_ans));
  CONDSUB8 condsub8_8 (.A(condsub8_7_ans), .B(B), .sign(bit_extender_1_out[0]), .Q(condsub8_8_q[0]), .ans(Remainder));
  Multiplexer #(.enable("false"), .width(8)) multiplexer_1 (
    .in0(condsub8_8_q), .in1({8{1'b0}}), .out(Quotient), .sel(comparator_1_eq));
endmodule

module CONDSUB8 (
  input  sign,
  input  [7:0] A,
  input  [7:0] B,
  output [7:0] ans,
  output Q
);

  wire comparator_1_lt;
  wire [8:0] bit_extender_1_out, bit_extender_2_out, multiplexer_1_out, shifter_1_out, subtractor_1_out;

  assign bit_extender_1_out = {{1{sign}}, A};  // Bit_Extender bit_extender_1
  assign bit_extender_2_out = {{1{1'b0}}, B};  // Bit_Extender bit_extender_2
  Shifter #(.shift("rl"), .width(9)) shifter_1 (.in(bit_extender_1_out), .\dist (4'b0001), .out(shifter_1_out));
  Comparator #(.mode("unsigned"), .width(9)) comparator_1 (
    .a(shifter_1_out), .b(bit_extender_2_out), .lt(comparator_1_lt));  // open: gt, eq
  Subtractor #(.width(9)) subtractor_1 (
    .a(shifter_1_out), .b(bit_extender_2_out), .out(subtractor_1_out));  // open: bin, bout
  not not_1 (Q, comparator_1_lt);
  Multiplexer #(.enable("false"), .width(9)) multiplexer_1 (
    .in0(shifter_1_out), .in1(subtractor_1_out), .out(multiplexer_1_out), .sel(Q));
  Bit_Extender #(.in_width(9), .out_width(8), .\type ("zero")) bit_extender_3 (.in(multiplexer_1_out), .out(ans));
endmodule
