// Logisim project Мультиплексор.circ as structural Verilog: 2 circuits, main circuit main
module main (
  input  [3:0] A4,
  input  [3:0] A0,
  input  [3:0] A5,
  input  [3:0] A1,
  input  [3:0] A6,
  input  [3:0] A2,
  input  [3:0] A3,
  input  [3:0] A7,
  input  [2:0] S,
  output [3:0] B
);

  mux mux_1 (
    .S2(S[2]), .S1(S[1]), .S0(S[0]), .D0(A0[0]), .D1(A1[0]), .D2(A2[0]), .D3(A3[0]), .D4(A4[0]), .D5(A5[0]),
    .D6(A6[0]), .D7(A7[0]), .Y(B[0]));  // open: switch
  mux mux_2 (
    .S2(S[2]), .S1(S[1]), .S0(S[0]), .D0(A0[1]), .D1(A1[1]), .D2(A2[1]), .D3(A3[1]), .D4(A4[1]), .D5(A5[1]),
    .D6(A6[1]), .D7(A7[1]), .Y(B[1]));  // open: switch
  mux mux_3 (
    .S2(S[2]), .S1(S[1]), .S0(S[0]), .D0(A0[2]), .D1(A1[2]), .D2(A2[2]), .D3(A3[2]), .D4(A4[2]), .D5(A5[2]),
    .D6(A6[2]), .D7(A7[2]), .Y(B[2]));  // open: switch
  mux mux_4 (
    .S2(S[2]), .S1(S[1]), .S0(S[0]), .D0(A0[3]), .D1(A1[3]), .D2(A2[3]), .D3(A3[3]), .D4(A4[3]), .D5(A5[3]),
    .D6(A6[3]), .D7(A7[3]), .Y(B[3]));  // open: switch
endmodule

module mux (
  input  D0,
  input  D1,
  input  D2,
  input  D3,
  input  D4,
  input  D5,
  input  D6,
  input  D7,
  input  S2,
  input  S1,
  input  S0,
  input  switch,
  output Y
);

  wire and_1_out, and_2_out, and_3_out, and_4_out, and_5_out, and_6_out, and_7_out, and_8_out, not_1_out,
       not_2_out, not_3_out, not_4_out, not_5_out, not_6_out, not_7_out;

  not not_1 (not_1_out, S2);
  not not_2 (not_2_out, not_1_out);
  not not_3 (not_3_out, S1);
  not not_4 (not_4_out, not_3_out);
  not not_5 (not_5_out, S0);
  not not_6 (not_6_out, not_5_out);
  not not_7 (not_7_out, switch);
  and and_1 (and_1_out, D0, not_1_out, not_3_out, not_5_out, not_7_out);
  and and_2 (and_2_out, D1, not_1_out, not_3_out, not_6_out, not_7_out);
  and and_3 (and_3_out, D2, not_1_out, not_4_out, not_5_out, not_7_out);
  and and_4 (and_4_out, D3, not_1_out, not_4_out, not_6_out, not_7_out);
  or or_1 (Y, and_1_out, and_2_out, and_3_out, and_4_out, and_5_out, and_6_out, and_7_out, and_8_out);
  and and_5 (and_5_out, D4, not_2_out, not_3_out, not_5_out, not_7_out);
  and and_6 (and_6_out, D5, not_3_out, not_2_out, not_6_out, not_7_out);
  and and_7 (and_7_out, D6, not_4_out, not_2_out, not_5_out, not_7_out);
  and and_8 (and_8_out, D7, not_6_out, not_4_out, not_7_out, not_2_out);
endmodule
