// Logisim project Полусумматор 1b.circ as structural Verilog: 1 circuit, main circuit main
module main (
  input  A,
  input  B,
  output P,
  output S
);

  xor xor_1 (S, A, B);
  and and_1 (P, A, B);
endmodule
