// Logisim project Сумматор 1b.circ as structural Verilog: 1 circuit, main circuit main
module main (
  input  A,
  input  B,
  input  P0,
  output S,
  output P
);

  wire and_1_out, and_2_out, xor_1_out;

  and and_1 (and_1_out, A, B);
  xor xor_1 (xor_1_out, A, B);
  xor xor_2 (S, xor_1_out, P0);
  and and_2 (and_2_out, xor_1_out, P0);
  or or_1 (P, and_1_out, and_2_out);
endmodule
