// Logisim project Сумматор 8b.circ as structural Verilog: 2 circuits, main circuit main
module main (
  input  [7:0] A,
  input  [7:0] B,
  output [7:0] S
);

  wire sum_1_p, sum_2_p, sum_3_p, sum_4_p, sum_5_p, sum_6_p, sum_7_p, sum_8_p;

  sum sum_1 (.A(A[0]), .B(B[0]), .P0(1'b0), .S(S[0]), .P(sum_1_p));
  sum sum_2 (.A(A[4]), .B(B[4]), .P0(sum_7_p), .S(S[4]), .P(sum_2_p));
  sum sum_3 (.A(A[1]), .B(B[1]), .P0(sum_1_p), .S(S[1]), .P(sum_3_p));
  sum sum_4 (.A(A[5]), .B(B[5]), .P0(sum_2_p), .S(S[5]), .P(sum_4_p));
  sum sum_5 (.A(A[2]), .B(B[2]), .P0(sum_3_p), .S(S[2]), .P(sum_5_p));
  sum sum_6 (.A(A[6]), .B(B[6]), .P0(sum_4_p), .S(S[6]), .P(sum_6_p));
  sum sum_7 (.A(A[3]), .B(B[3]), .P0(sum_5_p), .S(S[3]), .P(sum_7_p));
  sum sum_8 (.A(A[7]), .B(B[7]), .P0(sum_6_p), .S(S[7]), .P(sum_8_p));
  LED led_1 (.in(sum_8_p));
endmodule

module sum (
  input  A,
  input  B,
  input  P0,
  output S,
  output P
);

  wire and_1_out, and_2_out, xor_1_out;

  and and_1 (and_1_out, A, B);
  xor xor_1 (xor_1_out, A, B);
  xor xor_2 (S, xor_1_out, P0);
  and and_2 (and_2_out, xor_1_out, P0);
  or or_1 (P, and_1_out, and_2_out);
endmodule
