// Logisim project Умножение 8b.circ as structural Verilog: 5 circuits, main circuit main
module main (
  input  [7:0] A,
  input  [7:0] B,
  output [15:0] C
);

  wire big_sum_1_c4, big_sum_1_s1, big_sum_1_s2, big_sum_1_s3, big_sum_1_s4, big_sum_1_s5, big_sum_1_s6,
       big_sum_1_s7, big_sum_2_c4, big_sum_2_s1, big_sum_2_s2, big_sum_2_s3, big_sum_2_s4, big_sum_2_s5,
       big_sum_2_s6, big_sum_2_s7, big_sum_3_c4, big_sum_3_s1, big_sum_3_s2, big_sum_3_s3, big_sum_3_s4,
       big_sum_3_s5, big_sum_3_s6, big_sum_3_s7, big_sum_4_c4, big_sum_4_s1, big_sum_4_s2, big_sum_4_s3,
       big_sum_4_s4, big_sum_4_s5, big_sum_4_s6, big_sum_4_s7, big_sum_5_c4, big_sum_5_s1, big_sum_5_s2,
       big_sum_5_s3, big_sum_5_s4, big_sum_5_s5, big_sum_5_s6, big_sum_5_s7, big_sum_6_c4, big_sum_6_s1,
       big_sum_6_s2, big_sum_6_s3, big_sum_6_s4, big_sum_6_s5, big_sum_6_s6, big_sum_6_s7, bitselector_1_out,
       bitselector_2_out, part_1_a0b1, part_1_a0b2, part_1_a0b3, part_1_a0b4, part_1_a0b5, part_1_a0b6,
       part_1_a0b7, part_1_a1b0, part_1_a1b1, part_1_a1b2, part_1_a1b3, part_1_a1b4, part_1_a1b5,
       part_1_a1b6, part_1_a1b7, part_1_a2b0, part_1_a2b1, part_1_a2b2, part_1_a2b3, part_1_a2b4,
       part_1_a2b5, part_1_a2b6, part_1_a2b7, part_1_a3b0, part_1_a3b1, part_1_a3b2, part_1_a3b3,
       part_1_a3b4, part_1_a3b5, part_1_a3b6, part_1_a3b7, part_1_a4b0, part_1_a4b1, part_1_a4b2,
       part_1_a4b3, part_1_a4b4, part_1_a4b5, part_1_a4b6, part_1_a4b7, part_1_a5b0, part_1_a5b1,
       part_1_a5b2, part_1_a5b3, part_1_a5b4, part_1_a5b5, part_1_a5b6, part_1_a5b7, part_1_a6b0,
       part_1_a6b1, part_1_a6b2, part_1_a6b3, part_1_a6b4, part_1_a6b5, part_1_a6b6, part_1_a6b7,
       part_1_a7b0, part_1_a7b1, part_1_a7b2, part_1_a7b3, part_1_a7b4, part_1_a7b5, part_1_a7b6,
       part_1_a7b7, xor_1_out;
  wire [7:0] inv8_1_b, inv8_2_b;
  wire [15:0] negator_1_out, part_1_a0b0;

  inv8 inv8_1 (.A(A), .B(inv8_1_b));
  inv8 inv8_2 (.A(B), .B(inv8_2_b));
  BitSelector bitselector_1 (.in(B), .out(bitselector_1_out), .sel(3'b111));
  BitSelector bitselector_2 (.in(A), .out(bitselector_2_out), .sel(3'b111));
  part part_1 (
    .B(inv8_2_b), .A(inv8_1_b), .a3b0(part_1_a3b0), .a3b1(part_1_a3b1), .a3b2(part_1_a3b2),
    .a3b3(part_1_a3b3), .a3b4(part_1_a3b4), .a3b5(part_1_a3b5), .a3b6(part_1_a3b6), .a3b7(part_1_a3b7),
    .a2b0(part_1_a2b0), .a2b1(part_1_a2b1), .a2b2(part_1_a2b2), .a2b3(part_1_a2b3), .a2b4(part_1_a2b4),
    .a2b5(part_1_a2b5), .a2b6(part_1_a2b6), .a2b7(part_1_a2b7), .a1b0(part_1_a1b0), .a1b1(part_1_a1b1),
    .a1b2(part_1_a1b2), .a1b3(part_1_a1b3), .a1b4(part_1_a1b4), .a1b5(part_1_a1b5), .a1b6(part_1_a1b6),
    .a1b7(part_1_a1b7), .a0b0(part_1_a0b0[0]), .a0b1(part_1_a0b1), .a0b2(part_1_a0b2), .a0b3(part_1_a0b3),
    .a0b4(part_1_a0b4), .a0b5(part_1_a0b5), .a0b6(part_1_a0b6), .a0b7(part_1_a0b7), .a7b0(part_1_a7b0),
    .a7b1(part_1_a7b1), .a7b2(part_1_a7b2), .a7b3(part_1_a7b3), .a7b4(part_1_a7b4), .a7b5(part_1_a7b5),
    .a7b6(part_1_a7b6), .a7b7(part_1_a7b7), .a6b0(part_1_a6b0), .a6b1(part_1_a6b1), .a6b2(part_1_a6b2),
    .a6b3(part_1_a6b3), .a6b4(part_1_a6b4), .a6b5(part_1_a6b5), .a6b6(part_1_a6b6), .a6b7(part_1_a6b7),
    .a5b0(part_1_a5b0), .a5b1(part_1_a5b1), .a5b2(part_1_a5b2), .a5b3(part_1_a5b3), .a5b4(part_1_a5b4),
    .a5b5(part_1_a5b5), .a5b6(part_1_a5b6), .a5b7(part_1_a5b7), .a4b0(part_1_a4b0), .a4b1(part_1_a4b1),
    .a4b2(part_1_a4b2), .a4b3(part_1_a4b3), .a4b4(part_1_a4b4), .a4b5(part_1_a4b5), .a4b6(part_1_a4b6),
    .a4b7(part_1_a4b7));
  xor xor_1 (xor_1_out, bitselector_1_out, bitselector_2_out);
  Multiplexer #(.enable("false"), .width(16)) multiplexer_1 (
    .in0(part_1_a0b0), .in1(negator_1_out), .out(C), .sel(xor_1_out));
  Negator #(.width(16)) negator_1 (.in(part_1_a0b0), .out(negator_1_out));
  big_sum big_sum_1 (
    .A7(1'b0), .A6(part_1_a7b0), .A5(part_1_a6b0), .A4(part_1_a5b0), .A3(part_1_a4b0), .A2(part_1_a3b0),
    .A1(part_1_a2b0), .A0(part_1_a1b0), .B7(part_1_a7b1), .B6(part_1_a6b1), .B5(part_1_a5b1),
    .B4(part_1_a4b1), .B3(part_1_a3b1), .B2(part_1_a2b1), .B1(part_1_a1b1), .B0(part_1_a0b1),
    .S0(part_1_a0b0[1]), .S1(big_sum_1_s1), .S2(big_sum_1_s2), .S3(big_sum_1_s3), .S4(big_sum_1_s4),
    .S5(big_sum_1_s5), .S6(big_sum_1_s6), .S7(big_sum_1_s7), .C4(big_sum_1_c4));  // open: C0
  big_sum big_sum_2 (
    .A7(big_sum_1_c4), .A6(big_sum_1_s7), .A5(big_sum_1_s6), .A4(big_sum_1_s5), .A3(big_sum_1_s4),
    .A2(big_sum_1_s3), .A1(big_sum_1_s2), .A0(big_sum_1_s1), .B7(part_1_a7b2), .B6(part_1_a6b2),
    .B5(part_1_a5b2), .B4(part_1_a4b2), .B3(part_1_a3b2), .B2(part_1_a2b2), .B1(part_1_a1b2),
    .B0(part_1_a0b2), .S0(part_1_a0b0[2]), .S1(big_sum_2_s1), .S2(big_sum_2_s2), .S3(big_sum_2_s3),
    .S4(big_sum_2_s4), .S5(big_sum_2_s5), .S6(big_sum_2_s6), .S7(big_sum_2_s7), .C4(big_sum_2_c4));  // open: C0
  big_sum big_sum_3 (
    .A7(big_sum_2_c4), .A6(big_sum_2_s7), .A5(big_sum_2_s6), .A4(big_sum_2_s5), .A3(big_sum_2_s4),
    .A2(big_sum_2_s3), .A1(big_sum_2_s2), .A0(big_sum_2_s1), .B7(part_1_a7b3), .B6(part_1_a6b3),
    .B5(part_1_a5b3), .B4(part_1_a4b3), .B3(part_1_a3b3), .B2(part_1_a2b3), .B1(part_1_a1b3),
    .B0(part_1_a0b3), .S0(part_1_a0b0[3]), .S1(big_sum_3_s1), .S2(big_sum_3_s2), .S3(big_sum_3_s3),
    .S4(big_sum_3_s4), .S5(big_sum_3_s5), .S6(big_sum_3_s6), .S7(big_sum_3_s7), .C4(big_sum_3_c4));  // open: C0
  big_sum big_sum_4 (
    .A7(big_sum_3_c4), .A6(big_sum_3_s7), .A5(big_sum_3_s6), .A4(big_sum_3_s5), .A3(big_sum_3_s4),
    .A2(big_sum_3_s3), .A1(big_sum_3_s2), .A0(big_sum_3_s1), .B7(part_1_a7b4), .B6(part_1_a6b4),
    .B5(part_1_a5b4), .B4(part_1_a4b4), .B3(part_1_a3b4), .B2(part_1_a2b4), .B1(part_1_a1b4),
    .B0(part_1_a0b4), .S0(part_1_a0b0[4]), .S1(big_sum_4_s1), .S2(big_sum_4_s2), .S3(big_sum_4_s3),
    .S4(big_sum_4_s4), .S5(big_sum_4_s5), .S6(big_sum_4_s6), .S7(big_sum_4_s7), .C4(big_sum_4_c4));  // open: C0
  big_sum big_sum_5 (
    .A7(big_sum_4_c4), .A6(big_sum_4_s7), .A5(big_sum_4_s6), .A4(big_sum_4_s5), .A3(big_sum_4_s4),
    .A2(big_sum_4_s3), .A1(big_sum_4_s2), .A0(big_sum_4_s1), .B7(part_1_a7b5), .B6(part_1_a6b5),
    .B5(part_1_a5b5), .B4(part_1_a4b5), .B3(part_1_a3b5), .B2(part_1_a2b5), .B1(part_1_a1b5),
    .B0(part_1_a0b5), .S0(part_1_a0b0[5]), .S1(big_sum_5_s1), .S2(big_sum_5_s2), .S3(big_sum_5_s3),
    .S4(big_sum_5_s4), .S5(big_sum_5_s5), .S6(big_sum_5_s6), .S7(big_sum_5_s7), .C4(big_sum_5_c4));  // open: C0
  big_sum big_sum_6 (
    .A7(big_sum_5_c4), .A6(big_sum_5_s7), .A5(big_sum_5_s6), .A4(big_sum_5_s5), .A3(big_sum_5_s4),
    .A2(big_sum_5_s3), .A1(big_sum_5_s2), .A0(big_sum_5_s1), .B7(part_1_a7b6), .B6(part_1_a6b6),
    .B5(part_1_a5b6), .B4(part_1_a4b6), .B3(part_1_a3b6), .B2(part_1_a2b6), .B1(part_1_a1b6),
    .B0(part_1_a0b6), .S0(part_1_a0b0[6]), .S1(big_sum_6_s1), .S2(big_sum_6_s2), .S3(big_sum_6_s3),
    .S4(big_sum_6_s4), .S5(big_sum_6_s5), .S6(big_sum_6_s6), .S7(big_sum_6_s7), .C4(big_sum_6_c4));  // open: C0
  big_sum big_sum_7 (
    .A7(big_sum_6_c4), .A6(big_sum_6_s7), .A5(big_sum_6_s6), .A4(big_sum_6_s5), .A3(big_sum_6_s4),
    .A2(big_sum_6_s3), .A1(big_sum_6_s2), .A0(big_sum_6_s1), .B7(part_1_a7b7), .B6(part_1_a6b7),
    .B5(part_1_a5b7), .B4(part_1_a4b7), .B3(part_1_a3b7), .B2(part_1_a2b7), .B1(part_1_a1b7),
    .B0(part_1_a0b7), .S0(part_1_a0b0[7]), .S1(part_1_a0b0[8]), .S2(part_1_a0b0[9]), .S3(part_1_a0b0[10]),
    .S4(part_1_a0b0[11]), .S5(part_1_a0b0[12]), .S6(part_1_a0b0[13]), .S7(part_1_a0b0[14]),
    .C4(part_1_a0b0[15]));  // open: C0
endmodule

module sum (
  input  A,
  input  B,
  input  P0,
  output S,
  output P
);

  wire and_1_out, and_2_out, xor_1_out;

  and and_1 (and_1_out, A, B);
  xor xor_1 (xor_1_out, A, B);
  xor xor_2 (S, xor_1_out, P0);
  and and_2 (and_2_out, xor_1_out, P0);
  or or_1 (P, and_1_out, and_2_out);
endmodule

module big_sum (
  input  A7,
  input  A6,
  input  A5,
  input  A4,
  input  A3,
  input  A2,
  input  A1,
  input  A0,
  input  C0,
  input  B7,
  input  B6,
  input  B5,
  input  B4,
  input  B3,
  input  B2,
  input  B1,
  input  B0,
  output S0,
  output S1,
  output S2,
  output S3,
  output S4,
  output S5,
  output S6,
  output S7,
  output C4
);

  wire sum_1_p, sum_2_p, sum_3_p, sum_4_p, sum_5_p, sum_6_p, sum_7_p;

  sum sum_1 (.A(A0), .B(B0), .P0(C0), .S(S0), .P(sum_1_p));
  sum sum_2 (.A(A4), .B(B4), .P0(sum_7_p), .S(S4), .P(sum_2_p));
  sum sum_3 (.A(A1), .B(B1), .P0(sum_1_p), .S(S1), .P(sum_3_p));
  sum sum_4 (.A(A5), .B(B5), .P0(sum_2_p), .S(S5), .P(sum_4_p));
  sum sum_5 (.A(A2), .B(B2), .P0(sum_3_p), .S(S2), .P(sum_5_p));
  sum sum_6 (.A(A6), .B(B6), .P0(sum_4_p), .S(S6), .P(sum_6_p));
  sum sum_7 (.A(A3), .B(B3), .P0(sum_5_p), .S(S3), .P(sum_7_p));
  sum sum_8 (.A(A7), .B(B7), .P0(sum_6_p), .S(S7), .P(C4));
  LED led_1 (.in(C4));
endmodule

module part (
  input  [7:0] B,
  input  [7:0] A,
  output a3b0,
  output a3b1,
  output a3b2,
  output a3b3,
  output a3b4,
  output a3b5,
  output a3b6,
  output a3b7,
  output a2b0,
  output a2b1,
  output a2b2,
  output a2b3,
  output a2b4,
  output a2b5,
  output a2b6,
  output a2b7,
  output a1b0,
  output a1b1,
  output a1b2,
  output a1b3,
  output a1b4,
  output a1b5,
  output a1b6,
  output a1b7,
  output a0b0,
  output a0b1,
  output a0b2,
  output a0b3,
  output a0b4,
  output a0b5,
  output a0b6,
  output a0b7,
  output a7b0,
  output a7b1,
  output a7b2,
  output a7b3,
  output a7b4,
  output a7b5,
  output a7b6,
  output a7b7,
  output a6b0,
  output a6b1,
  output a6b2,
  output a6b3,
  output a6b4,
  output a6b5,
  output a6b6,
  output a6b7,
  output a5b0,
  output a5b1,
  output a5b2,
  output a5b3,
  output a5b4,
  output a5b5,
  output a5b6,
  output a5b7,
  output a4b0,
  output a4b1,
  output a4b2,
  output a4b3,
  output a4b4,
  output a4b5,
  output a4b6,
  output a4b7
);

  and and_1 (a0b0, B[0], A[0]);
  and and_2 (a1b0, B[0], A[1]);
  and and_3 (a2b0, B[0], A[2]);
  and and_4 (a3b0, B[0], A[3]);
  and and_5 (a4b0, B[0], A[4]);
  and and_6 (a5b0, B[0], A[5]);
  and and_7 (a6b0, B[0], A[6]);
  and and_8 (a7b0, B[0], A[7]);
  and and_9 (a0b1, B[1], A[0]);
  and and_10 (a1b1, B[1], A[1]);
  and and_11 (a2b1, B[1], A[2]);
  and and_12 (a3b1, B[1], A[3]);
  and and_13 (a4b1, B[1], A[4]);
  and and_14 (a5b1, B[1], A[5]);
  and and_15 (a6b1, B[1], A[6]);
  and and_16 (a7b1, B[1], A[7]);
  and and_17 (a0b2, B[2], A[0]);
  and and_18 (a1b2, B[2], A[1]);
  and and_19 (a2b2, B[2], A[2]);
  and and_20 (a3b2, B[2], A[3]);
  and and_21 (a4b2, B[2], A[4]);
  and and_22 (a5b2, B[2], A[5]);
  and and_23 (a6b2, B[2], A[6]);
  and and_24 (a7b2, B[2], A[7]);
  and and_25 (a0b3, B[3], A[0]);
  and and_26 (a1b3, B[3], A[1]);
  and and_27 (a2b3, B[3], A[2]);
  and and_28 (a3b3, B[3], A[3]);
  and and_29 (a4b3, B[3], A[4]);
  and and_30 (a5b3, B[3], A[5]);
  and and_31 (a6b3, B[3], A[6]);
  and and_32 (a7b3, B[3], A[7]);
  and and_33 (a0b4, B[4], A[0]);
  and and_34 (a1b4, B[4], A[1]);
  and and_35 (a2b4, B[4], A[2]);
  and and_36 (a3b4, B[4], A[3]);
  and and_37 (a4b4, B[4], A[4]);
  and and_38 (a5b4, B[4], A[5]);
  and and_39 (a6b4, B[4], A[6]);
  and and_40 (a7b4, B[4], A[7]);
  and and_41 (a0b5, B[5], A[0]);
  and and_42 (a1b5, B[5], A[1]);
  and and_43 (a2b5, B[5], A[2]);
  and and_44 (a3b5, B[5], A[3]);
  and and_45 (a4b5, B[5], A[4]);
  and and_46 (a5b5, B[5], A[5]);
  and and_47 (a6b5, B[5], A[6]);
  and and_48 (a7b5, B[5], A[7]);
  and and_49 (a0b6, B[6], A[0]);
  and and_50 (a1b6, B[6], A[1]);
  and and_51 (a2b6, B[6], A[2]);
  and and_52 (a3b6, B[6], A[3]);
  and and_53 (a4b6, B[6], A[4]);
  and and_54 (a5b6, B[6], A[5]);
  and and_55 (a6b6, B[6], A[6]);
  and and_56 (a7b6, B[6], A[7]);
  and and_57 (a0b7, B[7], A[0]);
  and and_58 (a1b7, B[7], A[1]);
  and and_59 (a2b7, B[7], A[2]);
  and and_60 (a3b7, B[7], A[3]);
  and and_61 (a4b7, B[7], A[4]);
  and and_62 (a5b7, B[7], A[5]);
  and and_63 (a6b7, B[7], A[6]);
  and and_64 (a7b7, B[7], A[7]);
endmodule

module inv8 (
  input  [7:0] A,
  output [7:0] B
);

  wire [7:0] xor_8_out;

  xor xor_1 (xor_8_out[7], A[7], A[7]);
  xor xor_2 (xor_8_out[5], A[5], A[7]);
  xor xor_3 (xor_8_out[6], A[6], A[7]);
  xor xor_4 (xor_8_out[3], A[3], A[7]);
  xor xor_5 (xor_8_out[4], A[4], A[7]);
  xor xor_6 (xor_8_out[1], A[1], A[7]);
  xor xor_7 (xor_8_out[2], A[2], A[7]);
  xor xor_8 (xor_8_out[0], A[0], A[7]);
  big_sum big_sum_1 (
    .A7(xor_8_out[7]), .A6(xor_8_out[6]), .A5(xor_8_out[5]), .A4(xor_8_out[4]), .A3(xor_8_out[3]),
    .A2(xor_8_out[2]), .A1(xor_8_out[1]), .A0(xor_8_out[0]), .B0(A[7]), .S0(B[0]), .S1(B[1]), .S2(B[2]),
    .S3(B[3]), .S4(B[4]), .S5(B[5]), .S6(B[6]), .S7(B[7]));  // open: C0, B7, B6, B5, B4, B3, B2, B1, C4
endmodule
